# Fritzing sketch Schematic (saved by Fritzing 0.9.6b)
breadboards: 1

parts:
  J2 = Piezo Speaker
  U7 = MAX6675 [package=so08]
  CPU1 = NodeMCU WROOM ESP 32
  M1 = HT1621 LCD Display Module
  U8 = TRANSISTOR_NPN_2 [package=to-92]
  R8 = Resistor [tolerance=±5% resistance=680 package="0603 [SMD]"]
  R9 = Resistor [tolerance=±5% resistance=680 package="0603 [SMD]"]
  R10 = Resistor [tolerance=±5% resistance=680 package="0603 [SMD]"]
  U9 = TRANSISTOR_NPN_2 [package=to-92]
  U10 = TRANSISTOR_NPN_2 [package=to-92]
  Mod1 = generic-ac-power-supply [package=THT]
  RY1 = SSR-40VA
  RY2 = SSR-40VA
  R11 = Resistor [tolerance=±5% resistance=680 package="0603 [SMD]"]
  R12 = Resistor [tolerance=±5% resistance=680 package="0603 [SMD]"]

nets:
  N1: J2.pin1, U8.C
  N2: J2.pin2, U7.VDD, CPU1.pin_16, M1.pin5, Mod1.pin3#2, RY1.Pin_4, RY2.Pin_4, R11.Pin_1, R12.Pin_1
  N3: U7.VSS, CPU1.pin_15, M1.pin4, U8.E, U9.E, U10.E, Mod1.pin3#3
  N4: U7.SCK, CPU1.pin_24
  N5: U7.CS, CPU1.pin_9, CPU1.pin_25, R8.Pin_0
  N6: U7.MISO, CPU1.pin_26
  N7: CPU1.pin_10, R10.Pin_1
  N8: CPU1.pin_11, R9.Pin_1
  N9: CPU1.pin_27, M1.pin1
  N10: CPU1.pin_30, M1.pin2
  N11: CPU1.pin_31, M1.pin3
  N12: U8.B, R8.Pin_1
  N13: R9.Pin_0, U10.B
  N14: R10.Pin_0, U9.B
  N15: U9.C, RY2.Pin_3, R12.Pin_0
  N16: U10.C, RY1.Pin_3, R11.Pin_0

custom parts:
  NodeMCU WROOM ESP 32: 30 pol Development Kit
  HT1621 LCD Display Module: HT1621 LCD Display Module.
  generic-ac-power-supply: Generic ac power supply module. Use as is, or customize the svgs to fit your particular device (as they are all different.) Provides AC input and single DC output. PCB is generic and will need modifications if you intend to do a pcb mount.
  SSR-40VA: SSR-40VA solid state relay.
